# Fritzing sketch Schema-Complet (saved by Fritzing 1.0.3b)

parts:
  A3 = Esp32-c3 super mini
  MOD1 = MT3608 Boost No usb
  D1 = Diode [package=diode-1n4001]
  D2 = Diode [package=diode-1n4001]
  C1 = Capacitor Polarized [package=panasonic_d]
  U1 = 2ChannelRelay
  C2 = Capacitor Polarized [package=panasonic_d]
  S1 = Square Pushbutton
  S2 = Square Pushbutton
  LED1 = LED - 5mm [color="Red (633nm)" current=0.030A package="5 mm [THT]"]
  R1 = Resistor [tolerance=±5% power=0.25W resistance=680 package=THT]
  ZS-042_RTC1 = ZS-042 RTC Module
  A4 = SM5308 battery charger module
  L1 = Solenoid
  BAT1 = Battery Holders [package=battery-aaa]
  S3 = Toggle Switch [package=THT]  # not connected
  LED2 = LED - 3mm [color="Red (633nm)" package="3 mm [THT]"]  # not connected
  LED3 = LED - 3mm [color="Blue (470nm)" current=0.030A package="3 mm [THT]"]  # not connected

nets:
  N1: A3.Pin_4, ZS-042_RTC1.SDA
  N2: A3.Pin_5, ZS-042_RTC1.SCL
  N3: A3.Pin_6, S1.leg0
  N4: A3.Pin_8, S2.leg0
  N5: A3.Pin_10, U1.connector3
  N6: A3.Pin_11, R1.Pin_1
  N7: A3.Pin_13, U1.connector2
  N8: A3.Pin_15, ZS-042_RTC1.GND
  N9: A3.Pin_16, A4.Pin_4
  N10: MOD1.IN_(-), MOD1.OUT_(-), U1.connector1, U1.connector5, U1.connector8, C2.-, S2.leg1, A4.Pin_1, A4.Pin_5, BAT1.-
  N11: MOD1.IN_(+), A4.Pin_2, BAT1.+
  N12: MOD1.OUT_(+), U1.connector6, U1.connector9, C2.+
  N13: D1.A, D2.C, U1.connector7
  N14: D1.C, D2.A, C1.+, L1.pin2
  N15: C1.-, U1.connector4, L1.pin1
  N16: U1.connector0, ZS-042_RTC1.VCC
  N17: S1.leg1, LED1.cathode
  N18: LED1.anode, R1.Pin_0

notes:
  Electro-Vanne
  1000 uF
  1N4007
  MT3608
  4.2V->5V
  680Ω
  AZdelivery
  RTC
  Batterie Lithium 18650
  18650 Porte-piles 3V Micro USB
  ESP32 C3-mini
  Momentané
  Optocoupler
  Poulet 2025
  Automator 2000 V1.0

custom parts:
  Esp32-c3 super mini: ESP32-C3 Development Board ESP32 SuperMini Development Board ESP32 Development Board WiFi Bluetooth.
  MT3608 Boost No usb: Chip- MT3608 / B6289 DC to DC step up, power booster module. With adjustable output voltage. Current- 2A . || Input voltage- 2V-24V || Output voltage- 5V-28V Input interface- Inversed polarity- NO. || Led indicator- No.
  SM5308 battery charger module: Charger module for Lipo Battery from Usb, 5v 2a, Sm5308 chip.

// code stored in the sketch: Untitled.ino
/* 
  ????????????????????????????????????????????????????????
  ?        MANUEL UTILISATEUR ? SANS DEEPSLEEP           ?
  ????????????????????????????????????????????????????????


  Description :
  ----------------
  Ce programme gère l?arrosage automatique via un ESP32 et une horloge RTC DS3231.
  Il permet de définir des plages horaires, un nombre de cycles d?arrosage, 
  une durée par cycle, et de tout configurer via un bouton physique ou une 
  interface web accessible en Wi-Fi local.


  Fonctionnalités :
  --------------------
  - Activation/désactivation de l'automatisme par bouton ou web
  - Arrosages répartis entre une heure de début et de fin
  - Configuration stockée dans l'EEPROM
  - Interface web locale via point d'accès Wi-Fi (durée limitée à 10 min)
  - LED d'état (RTC, Web, Vanne)


  Boutons physiques :
  ----------------------
  - Bouton AUTOMATISME (pin 21) :
      ? Appui court ? Active/Désactive l?automatisme
      ? Si désactivé et la vanne est ouverte ? fermeture immédiate


  - Bouton WEB (pin 10) :
      ? Appui court ? Active le point d?accès Wi-Fi ?arrosageESP?
        Mot de passe : secretESP32
        Durée : 10 minutes (désactivation automatique)


  LED d?état (pin 2) :
  -----------------------
  - Clignote RAPIDEMENT ? RTC absente ou non détectée
  - Clignote LENTEMENT ? Serveur web actif
  - Allumée FIXE ? Vanne actuellement ouverte
  - Éteinte ? Tout fonctionne normalement, vanne fermée


  Interface web :
  ------------------
  - Accessible à l?adresse http://192.168.4.1
  - Permet de configurer :
      ? Activation de l?automatisme
      ? Heure de début / fin
      ? Durée de chaque cycle (min)
      ? Nombre de cycles par jour
  - Données enregistrées automatiquement dans l?EEPROM


  Fonctionnement de l?arrosage :
  ---------------------------------
  - Si l?automatisme est activé :
      ? Le temps entre heure début et fin est découpé en ?nombre d?arrosages?
      ? À chaque instant prévu : impulsion d?ouverture de 200 ms
      ? Après la durée définie : impulsion de fermeture
      ? Si l?ESP est redémarré : la logique reprend son cours normalement


  Remarques :
  --------------
  - Le RTC doit être présent et à l?heure pour fonctionner correctement.
  - Le système n?arrose rien si l?automatisme est désactivé.
  - La configuration est conservée même après une coupure de courant.


  Dépendances :
  ----------------
  - Bibliothèques : WiFi.h, WebServer.h, DNSServer.h, RTClib.h, EEPROM.h
  - Matériel : ESP32, DS3231, relais (impulsionnels), boutons, LED


  Auteur : Jean-Sébastien ? L?Atelier Autonome
  Dernière mise à jour : mai 2025
*/



#include <WiFi.h>
#include <WebServer.h>
#include <DNSServer.h>
#include <Wire.h>
#include <RTClib.h>
#include <EEPROM.h>


// === Définition des broches ===
#define BUTTON_WEB_PIN     10   // bouton d'activation du serveur web
#define BUTTON_AUTO_PIN    21   // bouton enable/disable automatisme
#define RELAY_OPEN_PIN     4    // relais pour ouverture vanne (impulsion)
#define RELAY_CLOSE_PIN    1    // relais pour fermeture vanne (impulsion)
#define LED_PIN            2
#define SDAPIN             8
#define SCLPIN             9


// === Configuration EEPROM ===
#define EEPROM_SIZE 16
#define EEPROM_ADDR_ENABLED      0   // 1 octet (booléen)
#define EEPROM_ADDR_START_HOUR   1   // 1 octet
#define EEPROM_ADDR_END_HOUR     2   // 1 octet
#define EEPROM_ADDR_DURATION     3   // 1 octet
#define EEPROM_ADDR_NB_CYCLES    4   // 1 octet
#define EEPROM_ADDR_START_MIN   5   // minute début
#define EEPROM_ADDR_END_MIN     6   // minute fin


// === Configuration Réseau ===
const char* ssid = "arrosageESP";
const char* password = "secretESP32";
IPAddress local_IP(192, 168, 4, 1);
IPAddress gateway(192, 168, 4, 1);
IPAddress subnet(255, 255, 255, 0);


RTC_DS3231 rtc;
WebServer server(80);
DNSServer dnsServer;


bool rtcOk = false;
unsigned long webServerStartTime = 0;
const unsigned long WEB_SERVER_DURATION = 300000; // 5 min
bool webServerEnabled = false;


bool autoEnabled = true;
uint8_t heureDebut = 8;
uint8_t minuteDebut = 0;
uint8_t heureFin = 20;
uint8_t minuteFin = 0;


uint8_t dureeArrosage = 10;
uint8_t nombreArrosages = 12;


unsigned long dernierArrosage = 0;
bool vanneOuverte = false;


unsigned long ledTimer = 0;
bool ledState = false;




void updateLEDStatus() {
  if (!rtcOk) {
    // Clignotement rapide (RTC absente)
    if (millis() - ledTimer >= 250) {
      ledTimer = millis();
      ledState = !ledState;
      digitalWrite(LED_PIN, ledState);
    }
  } else if (webServerEnabled) {
    // Clignotement lent (serveur web actif)
    if (millis() - ledTimer >= 500) {
      ledTimer = millis();
      ledState = !ledState;
      digitalWrite(LED_PIN, ledState);
    }
  } else if (autoEnabled) {
    // LED fixe (automatisme actif)
    digitalWrite(LED_PIN, HIGH);
  } else {
    // LED éteinte (tout va bien, automatisme inactif)
    digitalWrite(LED_PIN, LOW);
  }
}




void saveConfigToEEPROM() {
  EEPROM.write(EEPROM_ADDR_ENABLED, autoEnabled);
  EEPROM.write(EEPROM_ADDR_START_HOUR, heureDebut);
  EEPROM.write(EEPROM_ADDR_START_MIN, minuteDebut);
  EEPROM.write(EEPROM_ADDR_END_HOUR, heureFin);
  EEPROM.write(EEPROM_ADDR_END_MIN, minuteFin);
  EEPROM.write(EEPROM_ADDR_DURATION, dureeArrosage);
  EEPROM.write(EEPROM_ADDR_NB_CYCLES, nombreArrosages);
  EEPROM.commit();
  Serial.println("Configuration enregistrée dans l'EEPROM.");
}


void loadConfigFromEEPROM() {
  autoEnabled     = EEPROM.read(EEPROM_ADDR_ENABLED);
  heureDebut      = EEPROM.read(EEPROM_ADDR_START_HOUR);
  minuteDebut     = EEPROM.read(EEPROM_ADDR_START_MIN);
  heureFin        = EEPROM.read(EEPROM_ADDR_END_HOUR);
  minuteFin       = EEPROM.read(EEPROM_ADDR_END_MIN);
  dureeArrosage   = EEPROM.read(EEPROM_ADDR_DURATION);
  nombreArrosages = EEPROM.read(EEPROM_ADDR_NB_CYCLES);
  Serial.println("Configuration chargée depuis l'EEPROM.");
}


void handlePhysicalButtons() {
  static bool lastAutoBtn = HIGH;
  static bool lastWebBtn = HIGH;


  bool autoBtn = digitalRead(BUTTON_AUTO_PIN);
  bool webBtn = digitalRead(BUTTON_WEB_PIN);


  if (lastAutoBtn == HIGH && autoBtn == LOW) {
    delay(20);
    if (digitalRead(BUTTON_AUTO_PIN) == LOW) {
      autoEnabled = !autoEnabled;
      saveConfigToEEPROM();
      Serial.printf("?? Automatisme %s\n", autoEnabled ? "activé" : "désactivé");
      if (!autoEnabled && vanneOuverte) {
        fermerVanne();
      }
    }
  }
  lastAutoBtn = autoBtn;


  if (lastWebBtn == HIGH && webBtn == LOW) {
    delay(20);
    if (digitalRead(BUTTON_WEB_PIN) == LOW && !webServerEnabled) {
      WiFi.mode(WIFI_AP);
      WiFi.softAPConfig(local_IP, gateway, subnet);
      WiFi.softAP(ssid, password);
      dnsServer.start(53, "", WiFi.softAPIP());
      server.begin();
      webServerEnabled = true;
      webServerStartTime = millis();
      Serial.println("?? Serveur web activé.");
    }
  }
  lastWebBtn = webBtn;
}



void setup() {
  Serial.begin(115200);
  delay(1000);


  pinMode(RELAY_OPEN_PIN, OUTPUT);
  pinMode(RELAY_CLOSE_PIN, OUTPUT);
  pinMode(LED_PIN, OUTPUT);
  pinMode(BUTTON_WEB_PIN, INPUT_PULLUP);
  pinMode(BUTTON_AUTO_PIN, INPUT_PULLUP);


  digitalWrite(RELAY_OPEN_PIN, HIGH);
  digitalWrite(RELAY_CLOSE_PIN, HIGH);
  digitalWrite(LED_PIN, LOW);


  Wire.begin(SDAPIN, SCLPIN);
  rtcOk = rtc.begin();
  if (!rtcOk) {
    Serial.println("Erreur : RTC non détectée !");
  } else {
    if (rtc.lostPower()) {
      rtc.adjust(DateTime(F(__DATE__), F(__TIME__)));
    }
  }


  EEPROM.begin(EEPROM_SIZE);


  loadConfigFromEEPROM();


  Serial.println("Configuration chargée :");
  Serial.printf(" - Automatisme : %s\n", autoEnabled ? "actif" : "inactif");
  Serial.printf(" - Heure début : %02d:%02d\n", heureDebut, minuteDebut);
  Serial.printf(" - Heure fin : %02d:%02d\n", heureFin, minuteFin);
  Serial.printf(" - Durée arrosage : %d min\n", dureeArrosage);
  Serial.printf(" - Nombre d'arrosages : %d\n", nombreArrosages);


  server.onNotFound([]() {
  server.sendHeader("Location", "/", true);
  server.send(302, "text/plain", "Redirecting to /");
});


server.on("/generate_204", []() {
  server.sendHeader("Location", "/", true);
  server.send(302, "text/plain", "");
});
server.on("/hotspot-detect.html", []() {
  server.sendHeader("Location", "/", true);
  server.send(302, "text/plain", "");
});
server.on("/ncsi.txt", []() {
  server.sendHeader("Location", "/", true);
  server.send(302, "text/plain", "");
});
server.on("/fwlink", []() {
  server.sendHeader("Location", "/", true);
  server.send(302, "text/plain", "");
});



   server.on("/", HTTP_GET, []() {
    String html = "<!DOCTYPE html><html><head><meta charset='UTF-8'><title>Arrosage</title><style>body{font-family:sans-serif;text-align:center;}input,select{padding:5px;margin:5px;}</style></head><body>";
    DateTime now = rtc.now();
    html += "<p>Heure actuelle RTC : <strong>" + String(now.hour()) + "h" + (now.minute() < 10 ? "0" : "") + String(now.minute()) + "</strong></p>";
    html += "<h1>Arrosage automatique</h1>";
    html += "<form action='/save' method='GET'>";
    html += "<label><input type='checkbox' name='enabled'" + String(autoEnabled ? " checked" : "") + "> Automatisme actif</label><br>";





    html += "Heure début: <select name='hd'>";
    for (int i = 0; i < 24; i++) html += "<option value='" + String(i) + "'" + (i == heureDebut ? " selected" : "") + ">" + String(i) + "</option>";
    html += "</select>:<select name='md'>";
    for (int i = 0; i < 60; i++) html += "<option value='" + String(i) + "'" + (i == minuteDebut ? " selected" : "") + ">" + String(i) + "</option>";
    html += "</select><br>";


    html += "Heure fin: <select name='hf'>";
    for (int i = 0; i < 24; i++) html += "<option value='" + String(i) + "'" + (i == heureFin ? " selected" : "") + ">" + String(i) + "</option>";
    html += "</select>:<select name='mf'>";
    for (int i = 0; i < 60; i++) html += "<option value='" + String(i) + "'" + (i == minuteFin ? " selected" : "") + ">" + String(i) + "</option>";
    html += "</select><br>";


    html += "</select><br>Durée (min): <select name='dur'>";
    int options[] = {10,15,20,30,45,60};
    for (int i = 0; i < 6; i++) html += "<option" + String(options[i] == dureeArrosage ? " selected" : "") + ">" + String(options[i]) + "</option>";
    html += "</select><br>Nombre arrosages: <select name='nb'>";
    for (int i = 1; i <= 24; i++) html += "<option" + String(i == nombreArrosages ? " selected" : "") + ">" + String(i) + "</option>";
    html += "</select><br><br><input type='submit' value='Enregistrer'>";
    html += "<hr>";


    // Ajout de l'affichage des heures de déclenchement programmées
int debutTotal = heureDebut * 60 + minuteDebut;
int finTotal = heureFin * 60 + minuteFin;
int plageTotale = finTotal - debutTotal;


if (plageTotale > 0 && nombreArrosages > 0) {
  float intervalle = (float)plageTotale / (float)nombreArrosages;
  html += "<hr><h3>Heures programmées :</h3><ul style='list-style:none;padding:0;'>";


  for (int i = 0; i < nombreArrosages; i++) {
    int minuteCible = debutTotal + round(i * intervalle);
    int h = minuteCible / 60;
    int m = minuteCible % 60;
    html += "<li>" + String(h) + "h" + (m < 10 ? "0" : "") + String(m) + "</li>";
  }


  html += "</ul>";
}
html += "</form>"; 
    html += "<hr><h3>Contrôle manuel (debug)</h3>";
    if (autoEnabled) {
      html += "<p>Automatisme actif : désactivez-le pour utiliser les boutons.</p>";
      html += "<button disabled>Ouvrir la vanne</button> ";
      html += "<button disabled>Fermer la vanne</button>";
    } else {
      html += "<form action='/open' method='GET' style='display:inline-block;margin:4px;'>";
      html += "<input type='submit' value='Ouvrir la vanne'></form>";
      html += "<form action='/close' method='GET' style='display:inline-block;margin:4px;'>";
      html += "<input type='submit' value='Fermer la vanne'></form>";
    }


    html += "<hr><h3>Régler l'heure de la RTC</h3>";
    html += "</form>";
    html += "<form action='/setrtc' method='GET'>";
    html += "Heure : <select name='h'>";
    for (int i = 0; i < 24; i++) html += "<option value='" + String(i) + "'>" + String(i) + "</option>";
    html += "</select> ";
    html += "Minute : <select name='m'>";
    for (int i = 0; i < 60; i++) html += "<option value='" + String(i) + "'>" + (i < 10 ? "0" : "") + String(i) + "</option>";
    html += "</select> ";
    html += "<input type='submit' value='Valider'>";


    html += "</form></body></html>";
    server.send(200, "text/html", html);
  });


  


  server.on("/save", HTTP_GET, []() {
    autoEnabled = server.hasArg("enabled");
    heureDebut = server.arg("hd").toInt();
    minuteDebut = server.arg("md").toInt();
    heureFin = server.arg("hf").toInt();
    minuteFin = server.arg("mf").toInt();
    dureeArrosage = server.arg("dur").toInt();
    nombreArrosages = server.arg("nb").toInt();


    EEPROM.write(EEPROM_ADDR_ENABLED, autoEnabled);
    EEPROM.write(EEPROM_ADDR_START_HOUR, heureDebut);
    EEPROM.write(EEPROM_ADDR_START_MIN, minuteDebut);
    EEPROM.write(EEPROM_ADDR_END_HOUR, heureFin);
    EEPROM.write(EEPROM_ADDR_END_MIN, minuteFin);
    EEPROM.write(EEPROM_ADDR_DURATION, dureeArrosage);
    EEPROM.write(EEPROM_ADDR_NB_CYCLES, nombreArrosages);
    EEPROM.commit();


    if (!autoEnabled && vanneOuverte) fermerVanne();


    server.sendHeader("Location", "/", true);
    server.send(302, "text/plain", "Redirection");
  });



  server.on("/setrtc", HTTP_GET, []() {
    if (server.hasArg("h") && server.hasArg("m")) {
      int newH = server.arg("h").toInt();
      int newM = server.arg("m").toInt();


      DateTime now = rtc.now();
      DateTime newTime(now.year(), now.month(), now.day(), newH, newM, 0);
      rtc.adjust(newTime);


      Serial.printf("?? Nouvelle heure RTC réglée : %02d:%02d\n", newH, newM);
    }


    server.sendHeader("Location", "/", true);
    server.send(302, "text/plain", "Redirection");
  });


  


    server.on("/open", HTTP_GET, []() {
    if (!autoEnabled) {
      if (!vanneOuverte) {
        Serial.println("?? Ouverture manuelle via Web");
        ouvrirVanne();
        // NOTE: en mode debug, on laisse ouvert tant que l'utilisateur ne reclique pas "Fermer".
      }
    }
    server.sendHeader("Location", "/", true);
    server.send(302, "text/plain", "");
  });


  server.on("/close", HTTP_GET, []() {
    if (!autoEnabled) {
      if (vanneOuverte) {
        Serial.println("?? Fermeture manuelle via Web");
        fermerVanne();
      }
    }
    server.sendHeader("Location", "/", true);
    server.send(302, "text/plain", "");
  });



  server.onNotFound([]() {
    server.send(404, "text/plain", "Page non trouvée");
  });
}  


void ouvrirVanne() {
  Serial.println("?? Ouverture de la vanne (impulsion 200 ms)");
  digitalWrite(RELAY_CLOSE_PIN, HIGH); // sécurité
  digitalWrite(RELAY_OPEN_PIN, LOW);
  delay(200);
  digitalWrite(RELAY_OPEN_PIN, HIGH);
  vanneOuverte = true;
}


void fermerVanne() {
  Serial.println("?? Fermeture de la vanne (impulsion 200 ms)");
  digitalWrite(RELAY_OPEN_PIN, HIGH); // sécurité
  digitalWrite(RELAY_CLOSE_PIN, LOW);
  delay(200);
  digitalWrite(RELAY_CLOSE_PIN, HIGH);
  vanneOuverte = false;
}


void loop() {


  updateLEDStatus();


  if (webServerEnabled) {
    server.handleClient();
    dnsServer.processNextRequest();
    if (millis() - webServerStartTime > WEB_SERVER_DURATION) {
      Serial.println("Serveur web désactivé automatiquement.");
      server.stop();
      WiFi.softAPdisconnect(true);
      webServerEnabled = false;
    }
  }


  static bool lastAutoButtonState = HIGH;
  bool currentAutoButton = digitalRead(BUTTON_AUTO_PIN);
  if (lastAutoButtonState == HIGH && currentAutoButton == LOW) {
    delay(20);
    if (digitalRead(BUTTON_AUTO_PIN) == LOW) {
      autoEnabled = !autoEnabled;
      EEPROM.write(EEPROM_ADDR_ENABLED, autoEnabled);
      EEPROM.commit();
      Serial.printf("Automatisme désormais %s\n", autoEnabled ? "activé" : "désactivé");
      if (!autoEnabled && vanneOuverte) {
        fermerVanne();
      }
    }
  }
  lastAutoButtonState = currentAutoButton;


  static bool lastWebButtonState = HIGH;
  bool currentWebButton = digitalRead(BUTTON_WEB_PIN);
  if (lastWebButtonState == HIGH && currentWebButton == LOW) {
    delay(20);
    if (digitalRead(BUTTON_WEB_PIN) == LOW && !webServerEnabled) {
      WiFi.mode(WIFI_AP);
      WiFi.softAPConfig(local_IP, gateway, subnet);
      WiFi.softAP(ssid, password);
      dnsServer.start(53, "*", WiFi.softAPIP());
      server.begin();
      webServerEnabled = true;
      webServerStartTime = millis();
      Serial.println("Serveur web démarré.");
    }
  }
  lastWebButtonState = currentWebButton;


  if (!autoEnabled || !rtcOk) return;


  DateTime now = rtc.now();
  int heureActuelle = now.hour();
  int minuteActuelle = now.minute();


  int debutTotal = heureDebut * 60 + minuteDebut;
  int finTotal = heureFin * 60 + minuteFin;


  int plageTotale = finTotal - debutTotal;
  if (plageTotale <= 0 || nombreArrosages == 0) return;


  float intervalle = (float)plageTotale / (float)nombreArrosages;


  int nowMinutes = now.hour() * 60 + now.minute();


  for (int i = 0; i < nombreArrosages; i++) {
    int minuteCible = debutTotal + round(i * intervalle);



    if (nowMinutes == minuteCible && !vanneOuverte) {
      ouvrirVanne();
      dernierArrosage = millis();
    }
  }


  if (vanneOuverte && millis() - dernierArrosage >= (unsigned long)dureeArrosage * 60000UL) {
    fermerVanne();
  }
  yield();  // ou delay(1);
}
