# Fritzing sketch PCB-Fritzing (saved by Fritzing 1.0.3b)
circuit board: 6.20633cm x 4.86934cm
breadboards: 1

parts:
  A1 = Esp32-c3 super mini
  End_Close = female pin header, 2 pins [form="♀ (female)"]
  End_Up = female pin header, 2 pins [form="♀ (female)"]
  LED1 = LED - 5mm [color="Yellow (595nm)" current=0.030A package="5 mm [THT]"]
  R1 = Resistor [tolerance=±5% power=0.25W resistance=220 package=THT]
  B_Close = female pin header, 2 pins [form="♀ (female)"]
  B_Up = female pin header, 2 pins [form="♀ (female)"]
  B_Close2 = female pin header, 4 pins [form="♀ (female)"]
  B_Close1 = female pin header, 2 pins [form="♀ (female)"]
  B_Close4 = female pin header, 4 pins [form="♀ (female)"]
  B_Close3 = female pin header, 6 pins [form="♀ (female)"]

nets:
  N1: A1.Pin_1, B_Close3.pin5
  N2: A1.Pin_4, B_Close3.pin3
  N3: A1.Pin_5, B_Close3.pin4
  N4: A1.Pin_6, B_Up.pin1
  N5: A1.Pin_8, B_Close.pin1
  N6: A1.Pin_9, End_Close.pin1
  N7: A1.Pin_10, B_Close2.pin3
  N8: A1.Pin_11, LED1.anode
  N9: A1.Pin_12, End_Up.pin1
  N10: A1.Pin_13, B_Close2.pin2
  N11: A1.Pin_15, End_Close.pin2, End_Up.pin2, R1.Pin_0, B_Close.pin2, B_Up.pin2, B_Close2.pin4, B_Close1.pin2, B_Close4.pin1, B_Close3.pin1
  N12: A1.Pin_16, B_Close2.pin1, B_Close1.pin1, B_Close4.pin2, B_Close3.pin2
  N13: LED1.cathode, R1.Pin_1

notes:
  SuperMini
  USB
  OpenDrop
  1.0
  JS NIEL
  32k
  SQW
  SCL
  SDA
  VCC
  GND
  2026
  ESP32 C3
  GPIO3
  GPIO0
  B-Autom
  B-Wifi
  IN2
  IN1
  5VIN
  RLYmodule
  68Ω
  RTC
  RedLed

custom parts:
  Esp32-c3 super mini: ESP32-C3 Development Board ESP32 SuperMini Development Board ESP32 Development Board WiFi Bluetooth.

// code stored in the sketch: Croquettor2.ino

